// Logisim project pr2.circ as structural Verilog: 1 circuit, main circuit main
module main (
  input  a,
  input  b,
  input  c,
  input  d,
  input  e,
  input  f,
  output x,
  output y,
  output z,
  output u,
  output v,
  output w,
  output s,
  output t
);

  wire not_1_out, not_2_out, not_3_out, not_4_out, not_5_out, not_6_out, not_7_out, not_8_out, not_9_out,
       not_10_out, not_11_out, not_12_out, not_13_out, not_14_out, not_15_out, not_16_out, not_17_out,
       not_18_out, not_19_out, not_20_out, not_21_out;

  not not_1 (not_1_out, a);
  not not_2 (not_2_out, b);
  not not_3 (not_3_out, c);
  not not_4 (not_4_out, d);
  not not_5 (not_5_out, a);
  not not_6 (not_6_out, b);
  not not_7 (not_7_out, c);
  not not_8 (not_8_out, d);
  not not_9 (not_9_out, a);
  not not_10 (not_10_out, c);
  not not_11 (not_11_out, d);
  not not_12 (not_12_out, a);
  not not_13 (not_13_out, d);
  not not_14 (not_14_out, b);
  not not_15 (not_15_out, c);
  not not_16 (not_16_out, d);
  not not_17 (not_17_out, b);
  not not_18 (not_18_out, d);
  not not_19 (not_19_out, b);
  not not_20 (not_20_out, d);
  not not_21 (not_21_out, d);
  or or_1 (x, not_1_out, not_2_out, not_3_out, not_4_out, e, f);
  or or_2 (y, not_5_out, not_6_out, not_7_out, not_8_out, e, f);
  or or_3 (z, not_9_out, not_10_out, b, not_11_out, e, f);
  or or_4 (u, not_12_out, c, b, not_13_out, e, f);
  or or_5 (v, not_14_out, not_15_out, a, not_16_out, e, f);
  or or_6 (w, not_17_out, c, a, not_18_out, e, f);
  or or_7 (s, not_19_out, c, a, not_20_out, e, f);
  or or_8 (t, c, b, a, not_21_out, e, f);

  // Notes on the sheet:
  //   PB20020586 叶子昂
  //   a,b,c分别为A2,A1,A0
  //   d,e,f分别为G1,G2,G3
  //   x到t分别为Y7到Y0
endmodule
