// Logisim project eg1.circ as structural Verilog: 14 circuits, main circuit main
module main (
  input  in_1,
  output out_2,
  output out_3
);

  not not_1 (out_2, out_3);
  not not_2 (out_3, out_2);
endmodule

module \S_R锁存器  (
  input  in_1,
  input  in_2,
  output out_3,
  output out_4
);

  wire or_1_out, or_2_out;

  or or_1 (or_1_out, in_1, out_4);
  or or_2 (or_2_out, out_3, in_2);
  not not_1 (out_3, or_1_out);
  not not_2 (out_4, or_2_out);
endmodule

module \D锁存器  (
  input  CLK,
  input  in_2,
  output out_3,
  output out_4
);

  wire and_1_out, and_2_out, not_1_out;

  and and_1 (and_1_out, CLK, not_1_out);
  not not_1 (not_1_out, in_2);
  and and_2 (and_2_out, CLK, in_2);
  \S_R锁存器  \s_r锁存器_1  (.in_1(and_1_out), .in_2(and_2_out), .out_3(out_3), .out_4(out_4));
endmodule

module \D触发器  (
  input  D,
  output Q,
  output out_3
);

  wire clock_1_out, \d锁存器_1_out_3 , not_1_out;

  Clock clock_1 (.out(clock_1_out));
  not not_1 (not_1_out, clock_1_out);
  \D锁存器  \d锁存器_1  (.in_2(D), .out_3(\d锁存器_1_out_3 ), .CLK(not_1_out));  // open: out_4
  \D锁存器  \d锁存器_2  (.in_2(\d锁存器_1_out_3 ), .out_3(Q), .out_4(out_3), .CLK(clock_1_out));
endmodule

module \同步复位  (
  input  D,
  input  reset,
  output Q,
  output out_4
);

  wire and_1_out, clock_1_out, \d锁存器_1_out_3 , not_1_out;

  Clock clock_1 (.out(clock_1_out));
  not not_1 (not_1_out, clock_1_out);
  and and_1 (and_1_out, D, reset);
  \D锁存器  \d锁存器_1  (.in_2(and_1_out), .out_3(\d锁存器_1_out_3 ), .CLK(not_1_out));  // open: out_4
  \D锁存器  \d锁存器_2  (.in_2(\d锁存器_1_out_3 ), .out_3(Q), .out_4(out_4), .CLK(clock_1_out));
endmodule

module \异步复位  (
  input  clk,
  input  D,
  input  reset,
  output Q,
  output out_5
);

  wire and_1_out, \d锁存器_1_out_3 , not_1_out, or_1_out;

  not not_1 (not_1_out, clk);
  \D锁存器  \d锁存器_1  (.in_2(D), .out_3(\d锁存器_1_out_3 ), .CLK(not_1_out));  // open: out_4
  or or_1 (or_1_out, clk, reset);
  and and_1 (and_1_out, \d锁存器_1_out_3 , ~reset);  // AND_Gate
  \D锁存器  \d锁存器_2  (.in_2(and_1_out), .out_3(Q), .out_4(out_5), .CLK(or_1_out));
endmodule

module \搭建寄存器  (
  input  [3:0] in_1,
  input  in_2,
  input  reset,
  input  [3:0] in_4
);

  wire and_1_out, and_2_out, and_3_out, and_4_out;

  and and_1 (and_1_out, reset, in_4[0]);
  and and_2 (and_2_out, reset, in_4[1]);
  and and_3 (and_3_out, reset, in_4[2]);
  and and_4 (and_4_out, reset, in_4[3]);
  \D触发器  \d触发器_1  (.D(and_1_out), .Q(in_1[0]));  // open: out_3
  \D触发器  \d触发器_2  (.D(and_2_out), .Q(in_1[1]));  // open: out_3
  \D触发器  \d触发器_3  (.D(and_3_out), .Q(in_1[2]));  // open: out_3
  \D触发器  \d触发器_4  (.D(and_4_out), .Q(in_1[3]));  // open: out_3
endmodule

module \搭建时序电路  (
);

  wire clock_1_out;

  Clock clock_1 (.out(clock_1_out));
  \搭建寄存器  \u_搭建寄存器_1  (.in_2(clock_1_out));  // open: reset, in_4, in_1
endmodule

module pr2 (
  input  D,
  input  ret,
  input  re_n,
  output Q,
  output out_5
);

  wire clock_1_out, \d锁存器_1_out_3 , not_1_out, \二选一_1_out_4 , \二选一_2_out_4 ;

  Clock clock_1 (.out(clock_1_out));
  not not_1 (not_1_out, clock_1_out);
  \二选一  \u_二选一_1  (.in_1(re_n), .in_2(D), .in_3(\二选一_2_out_4 ), .out_4(\二选一_1_out_4 ));
  \二选一  \u_二选一_2  (.in_1(ret), .in_2(1'b0), .in_3(1'b1), .out_4(\二选一_2_out_4 ));
  \D锁存器  \d锁存器_1  (.in_2(\二选一_1_out_4 ), .out_3(\d锁存器_1_out_3 ), .CLK(not_1_out));  // open: out_4
  \D锁存器  \d锁存器_2  (.in_2(\d锁存器_1_out_3 ), .out_3(Q), .out_4(out_5), .CLK(clock_1_out));
endmodule

module \二选一  (
  input  in_1,
  input  in_2,
  input  in_3,
  output out_4
);

  wire and_1_out, and_2_out, not_1_out;

  not not_1 (not_1_out, in_1);
  and and_1 (and_1_out, not_1_out, in_2);
  and and_2 (and_2_out, in_1, in_3);
  or or_1 (out_4, and_1_out, and_2_out);
endmodule

module pr3 (
  input  cp,
  output Q0,
  output Q1,
  output Q2,
  output out_5
);

  wire and_1_out, and_2_out, xor_1_out, xor_2_out, xor_3_out, xor_4_out;

  xor xor_1 (xor_1_out, 1'b1, Q0);
  \异步复位  \u_异步复位_1  (.D(xor_1_out), .reset(1'b0), .Q(Q0), .clk(cp));  // open: out_5
  xor xor_2 (xor_2_out, Q0, Q1);
  and and_1 (and_1_out, Q0, Q1);
  \异步复位  \u_异步复位_2  (.D(xor_2_out), .reset(1'b0), .Q(Q1), .clk(cp));  // open: out_5
  xor xor_3 (xor_3_out, and_1_out, Q2);
  and and_2 (and_2_out, and_1_out, Q2);
  \异步复位  \u_异步复位_3  (.D(xor_3_out), .reset(1'b0), .Q(Q2), .clk(cp));  // open: out_5
  xor xor_4 (xor_4_out, and_2_out, out_5);
  \异步复位  \u_异步复位_4  (.D(xor_4_out), .reset(1'b0), .Q(out_5), .clk(cp));  // open: out_5
endmodule

module pr4 (
  output Q0,
  output Q1,
  output Q2,
  output Q3
);

  wire and_1_out, and_2_out, clock_1_out, FF0_qn, FF1_qn, FF2_qn, multiplexer_2_out, not_1_out, \置位判断_out ;

  Clock clock_1 (.out(clock_1_out));
  not not_1 (not_1_out, clock_1_out);
  nor \u_置位判断  (\置位判断_out , Q0, Q1, Q2, Q3);
  T_Flip_Flop FF0 (.clk(not_1_out), .T(1'b1), .Q(Q0), .Qn(FF0_qn));  // open: preset, reset, en
  Multiplexer #(.enable("false")) multiplexer_1 (.in0(FF0_qn), .in1(1'b0), .sel(\置位判断_out ));  // open: out
  and and_1 (and_1_out, FF0_qn, FF1_qn);
  Multiplexer #(.enable("false")) multiplexer_2 (
    .in0(and_1_out), .in1(1'b0), .out(multiplexer_2_out), .sel(\置位判断_out ));
  T_Flip_Flop FF1 (.clk(not_1_out), .T(\置位判断_out ), .Q(Q1), .Qn(FF1_qn));  // open: preset, reset, en
  T_Flip_Flop FF2 (.clk(not_1_out), .T(multiplexer_2_out), .Q(Q2), .Qn(FF2_qn));  // open: preset, reset, en
  and and_2 (and_2_out, and_1_out, FF2_qn);
  T_Flip_Flop FF3 (.clk(not_1_out), .T(and_2_out), .Q(Q3));  // open: Qn, preset, reset, en
endmodule

module pr5 (
  input  D,
  input  reset,
  output Q,
  output out_4
);

  wire clock_1_out, \d锁存器_1_out_3 , not_1_out, not_2_out, or_1_out;

  Clock clock_1 (.out(clock_1_out));
  not not_1 (not_1_out, clock_1_out);
  or or_1 (or_1_out, ~D, reset);  // OR_Gate
  \D锁存器  \d锁存器_1  (.in_2(not_2_out), .out_3(\d锁存器_1_out_3 ), .CLK(not_1_out));  // open: out_4
  not not_2 (not_2_out, or_1_out);
  \D锁存器  \d锁存器_2  (.in_2(\d锁存器_1_out_3 ), .out_3(Q), .out_4(out_4), .CLK(clock_1_out));
endmodule

module pr6 (
  input  cp,
  output Q0,
  output Q1,
  output Q2,
  output out_5
);

  wire and_1_out, and_2_out, xor_1_out, xor_2_out, xor_3_out, xor_4_out;

  xor xor_1 (xor_1_out, 1'b1, Q0);
  \异步复位  \u_异步复位_1  (.D(xor_1_out), .reset(1'b0), .Q(Q0), .clk(cp));  // open: out_5
  xor xor_2 (xor_2_out, Q0, Q1);
  and and_1 (and_1_out, Q0, Q1);
  \异步复位  \u_异步复位_2  (.D(xor_2_out), .reset(1'b0), .Q(Q1), .clk(cp));  // open: out_5
  xor xor_3 (xor_3_out, and_1_out, Q2);
  and and_2 (and_2_out, and_1_out, Q2);
  \异步复位  \u_异步复位_3  (.D(xor_3_out), .reset(1'b0), .Q(Q2), .clk(cp));  // open: out_5
  xor xor_4 (xor_4_out, and_2_out, out_5);
  \异步复位  \u_异步复位_4  (.D(xor_4_out), .reset(1'b0), .Q(out_5), .clk(cp));  // open: out_5
endmodule
